# Fritzing sketch sensors_layout (saved by Fritzing 0.8.7b)
breadboards: 1

parts:
  Parte1 = Arduino Uno (Rev3)
  RHT1 = Humidity and Temperature Sensor RHT03
  Wind_vane_varistor = VARISTOR [package=0402-res]
  Tipping_bucket_gauge_switch = SWITCH-MOMENTARY-2 [package=tactile_switch_smd-2]
  Cup_anemometer_switch = SWITCH-MOMENTARY-2 [package=tactile_switch_smd-2]
  R1 = Resistor [package="2010 [SMD]"]
  R2 = Resistor [package="2010 [SMD]"]
  C1 = Ceramic Capacitor [capacitance=0.1mF package="100 mil [THT, multilayer]"]
  R3 = Resistor [package="2010 [SMD]"]
  Parte2 = Barometric Pressure Sensor - BMP085 Breakout

nets:
  N1: Parte1.A0, Wind_vane_varistor.2, R3.Pin_0
  GND: Parte1.GND, RHT1.GND_2, Wind_vane_varistor.1, Tipping_bucket_gauge_switch.1, Cup_anemometer_switch.1, Parte2.GND
  N2: Parte1.A4/SDA, Parte2.SDA
  N3: Parte1.A5/SCL, Parte2.SCL
  N4: Parte1.D2, R2.Pin_1, C1.1
  N5: Parte1.D3_PWM, Cup_anemometer_switch.2, R1.Pin_0
  N6: Parte1.D4, RHT1.Data-signal
  VCC: Parte1.5V, RHT1.Vcc, R1.Pin_1, C1.0, R3.Pin_1, Parte2.VCC
  5V: Parte1.VIN
  N7: Tipping_bucket_gauge_switch.2, R2.Pin_0

notes:
  Arduino Weather Station, Hookup layour for Arduino UNO and wind, rain, temperature, humidity and pressure sensors., 0.9

custom parts:
  Resistor: Resistor Basic schematic elements and footprints for 0603, 1206, and PTH resistors.
